# Fritzing sketch sketch (saved by Fritzing 1.0.6)
breadboards: 1

parts:
  Raspberry_Pi1 = Raspberry Pi B+
  Adafruit#1 = Adafruit ADS1115 16-Bit ADC [part_number=1085]
  AD1 = AD8232 ECG Module [part_number=AD8232]
  MAX1 = MAX30102 Pulse Oximeter [part_number=MAX30102]
  KY-1 = KY-016 3-Color RGB LED Module [part_number=KY-016]  # not connected
  KY-2 = KY-006 Passive Buzzer Module [part_number=KY-006]  # not connected
  KY-3 = KY-015 DHT11 Temperature and Humidity Sensor [part_number=KY-015]  # not connected

nets:
  3V3: Raspberry_Pi1.3v3, Raspberry_Pi1.3V3, AD1.3.3V, MAX1.VIN
  N1: Raspberry_Pi1.GPIO2, Adafruit#1.SDA, MAX1.SDA
  N2: Raspberry_Pi1.GPIO3, Adafruit#1.SCL, MAX1.SCL
  N3: Raspberry_Pi1.GPIO8, AD1.LO-
  N4: Raspberry_Pi1.GPIO25, AD1.LO+
  GND: Raspberry_Pi1.GND, AD1.GND, MAX1.GND
  N5: Adafruit#1.AIN0, AD1.OUTPUT

custom parts:
  AD8232 ECG Module: AD8232 single-lead ECG (electrocardiogram) heart rate monitor module. Outputs an analog signal proportional to the ECG waveform. Includes lead-off detection outputs (LO+, LO-) and a shutdown pin (SDN). Connect RA, LA, and RL electrode snaps to the corresponding body leads.
  MAX30102 Pulse Oximeter: MAX30102 pulse oximeter and heart rate monitor module. Uses I2C (address 0x57) to report SpO2 and heart rate data. Integrated red (660 nm) and infrared (880 nm) LEDs with optical sensor. Supply voltage 1.8–5 V via VIN. INT is an active-low interrupt output.
  KY-016 3-Color RGB LED Module: KY-016 3-color RGB LED module. Common cathode pin is marked -; drive R, G, and B individually.
  KY-006 Passive Buzzer Module: KY-006 passive piezo buzzer module. Drive S with a square wave or tone output; the middle header pin is typically not connected; - is GND.
  KY-015 DHT11 Temperature and Humidity Sensor: KY-015 DHT11 temperature and humidity sensor module. Pin order is S, +, - on common Keyes-style modules; always confirm the silkscreen on your board.
